// Logisim project hw4.circ as structural Verilog: 14 circuits, main circuit main
module main (
  input  reset,
  output [15:0] out_2
);

  wire BR, checkeq_1_out, checklt_1_out, clk, DMWe, equ, IN, iType, J, JAL, JR, keyboard_1_avail, less, nclk,
       or_1_out, OUT, Rdst, RWd, RWe;
  wire [2:0] multiplexer_9_out, multiplexer_10_out;
  wire [3:0] OpCode;
  wire [7:0] inpu;
  wire [11:0] Addr;
  wire [15:0] addsub_1_result, addsub_4_result, atAddr, imm_plus, iSum, multiplexer_1_out, multiplexer_2_out,
       multiplexer_3_out, multiplexer_4_out, multiplexer_7_out, multiplexer_8_out, multiplexer_11_out,
       pc_plus, ram_1_data, s, sImm, t;

  Multiplexer #(.select(4), .width(16), .enable("false")) multiplexer_1 (
    .in0(addsub_4_result), .in1(addsub_4_result), .in2(addsub_4_result), .in3(addsub_4_result),
    .in4(addsub_4_result), .in5(addsub_4_result), .in6(addsub_4_result), .in7(addsub_4_result),
    .in8(addsub_4_result), .in9(multiplexer_4_out), .in10(multiplexer_3_out), .in11(sImm), .in12(s),
    .in13(sImm), .in14(addsub_4_result), .in15(addsub_4_result), .out(multiplexer_1_out), .sel(OpCode));
  Multiplexer #(.width(16), .enable("false")) multiplexer_2 (
    .in0(multiplexer_1_out), .in1({16{1'b0}}), .out(multiplexer_2_out), .sel(reset));
  ctrl ctrl (
    .OpCode(OpCode), .Rwe(RWe), .J(J), .BR(BR), .DMwe(DMWe), .Rwd(RWd), .Rdst(Rdst), .IN(IN), .OUT(OUT),
    .JAL(JAL), .Itp(iType), .JR(JR));
  addsub addsub_1 (.result(addsub_1_result), .sub(1'b0), .A(sImm), .B(16'h1));  // open: ovf
  checklt checklt_1 (.in1(s), .in2(t), .out(checklt_1_out));
  checkeq checkeq_1 (.in1(s), .in2(t), .out(checkeq_1_out));
  Multiplexer #(.width(16), .enable("false")) multiplexer_3 (
    .in0(addsub_4_result), .in1(imm_plus), .out(multiplexer_3_out), .sel(less));
  Multiplexer #(.width(16), .enable("false")) multiplexer_4 (
    .in0(imm_plus), .in1(addsub_4_result), .out(multiplexer_4_out), .sel(equ));
  addsub addsub_2 (.result(pc_plus), .sub(1'b0), .A(out_2), .B(16'h1));  // open: ovf
  // Probe on imm_plus
  addsub addsub_3 (.result(imm_plus), .sub(1'b0), .A(out_2), .B(addsub_1_result));  // open: ovf
  Multiplexer #(.enable("false")) multiplexer_5 (.in0(1'b0), .in1(checklt_1_out), .out(less), .sel(BR));
  Multiplexer #(.enable("false")) multiplexer_6 (.in0(1'b0), .in1(checkeq_1_out), .out(equ), .sel(BR));
  addsub addsub_4 (.result(addsub_4_result), .sub(1'b0), .A(16'h1), .B(out_2));  // open: ovf
  register PC (.rIn(multiplexer_2_out), .clock(clk), .Reset(1'b0), .wEnable(1'b1), .rOut(out_2));
  ROM #(.addrWidth(16), .dataWidth(16)) rom_1 (.addr(out_2), .data({OpCode, Addr}));  // open: sel
  signextender signextender_1 (.immed(Addr[5:0]), .out(sImm));
  Clock clock_1 (.out(clk));
  not not_1 (nclk, clk);
  Keyboard keyboard_1 (.clk(clk), .re(IN), .clr(reset), .avail(keyboard_1_avail), .data(inpu[6:0]));
  Multiplexer #(.width(16), .enable("false")) multiplexer_7 (
    .in0(atAddr), .in1(pc_plus), .out(multiplexer_7_out), .sel(JAL));
  Multiplexer #(.width(16), .enable("false")) multiplexer_8 (
    .in0(multiplexer_7_out), .in1({{8{1'b0}}, inpu}), .out(multiplexer_8_out), .sel(IN));
  or or_1 (or_1_out, reset, RWe);
  Multiplexer #(.width(3), .enable("false")) multiplexer_9 (
    .in0(multiplexer_10_out), .in1(3'b111), .out(multiplexer_9_out), .sel(JAL));
  Multiplexer #(.width(3), .enable("false")) multiplexer_10 (
    .in0(Addr[5:3]), .in1(Addr[8:6]), .out(multiplexer_10_out), .sel(iType));
  not not_2 (inpu[7], keyboard_1_avail);
  RegisterFile RegFile (
    .reset(reset), .clk(nclk), .WriteData(multiplexer_8_out), .ReadReg1(Addr[11:9]), .ReadReg2(Addr[8:6]),
    .WE(or_1_out), .rd(multiplexer_9_out), .ReadData1(s), .ReadData2(t));
  // Probe on s
  Multiplexer #(.width(16), .enable("false")) multiplexer_11 (
    .in0(t), .in1(sImm), .out(multiplexer_11_out), .sel(iType));
  // Probe on s[6:0]
  TTY #(.rows(13), .cols(80), .trigger("falling")) tty_1 (.data(s[6:0]), .clk(clk), .we(OUT), .clr(reset));
  // Probe on multiplexer_11_out
  ALU ALU (.shAmt(Addr[2:0]), .InputData1(s), .InputData2(multiplexer_11_out), .OpCode(OpCode), .out(iSum));
  // Probe on iSum
  // Probe on t
  RAM #(.addrWidth(16), .dataWidth(16), .bus("separate")) ram_1 (
    .addr(iSum), .din(t), .data(ram_1_data), .str(DMWe), .clk(nclk));  // open: sel, ld, clr
  Multiplexer #(.width(16), .enable("false")) multiplexer_12 (.in0(iSum), .in1(ram_1_data), .out(atAddr), .sel(RWd));

  // Other names for the same wires on the sheet: Rest[11:0] = Addr; Rt[2:0] = Addr[8:6]; Rs[2:0] = Addr[11:9];
  //   Immed[5:0] = Addr[5:0]; Shamt[2:0] = Addr[2:0]; Rd[2:0] = Addr[5:3]; pc[15:0] = out_2; rst = reset

  // Notes on the sheet:
  //   CONTROL
  //   BRANCH PC MOVEMENT
  //   INSTRUCTION MEMORY, PC MANAGEMENT
  //   instruction iterator
  //   INSTRUCTION DECODING
  //   contents of rom_1 (hex, n*v repeats v):
  //   104f 108c 3418 4460 91ff 1fc1 91ff
  //   Register File
  //   INPUT/OUTPUT
  //   DATA MEMORY
endmodule

module register (
  input  [15:0] rIn,
  input  Reset,
  input  clock,
  input  wEnable,
  output [15:0] rOut
);

  wire [15:0] multiplexer_1_out;

  D_Flip_Flop d_ff_1 (.clk(clock), .D(multiplexer_1_out[15]), .Q(rOut[15]), .reset(Reset));  // open: Qn, preset, en
  D_Flip_Flop d_ff_2 (.clk(clock), .D(multiplexer_1_out[14]), .Q(rOut[14]), .reset(Reset));  // open: Qn, preset, en
  D_Flip_Flop d_ff_3 (.clk(clock), .D(multiplexer_1_out[13]), .Q(rOut[13]), .reset(Reset));  // open: Qn, preset, en
  D_Flip_Flop d_ff_4 (.clk(clock), .D(multiplexer_1_out[12]), .Q(rOut[12]), .reset(Reset));  // open: Qn, preset, en
  D_Flip_Flop d_ff_5 (.clk(clock), .D(multiplexer_1_out[11]), .Q(rOut[11]), .reset(Reset));  // open: Qn, preset, en
  D_Flip_Flop d_ff_6 (.clk(clock), .D(multiplexer_1_out[10]), .Q(rOut[10]), .reset(Reset));  // open: Qn, preset, en
  D_Flip_Flop d_ff_7 (.clk(clock), .D(multiplexer_1_out[9]), .Q(rOut[9]), .reset(Reset));  // open: Qn, preset, en
  Multiplexer #(.width(16), .enable("false")) multiplexer_1 (
    .in0(rOut), .in1(rIn), .out(multiplexer_1_out), .sel(wEnable));
  D_Flip_Flop d_ff_8 (.clk(clock), .D(multiplexer_1_out[8]), .Q(rOut[8]), .reset(Reset));  // open: Qn, preset, en
  D_Flip_Flop d_ff_9 (.clk(clock), .D(multiplexer_1_out[7]), .Q(rOut[7]), .reset(Reset));  // open: Qn, preset, en
  D_Flip_Flop d_ff_10 (.clk(clock), .D(multiplexer_1_out[6]), .Q(rOut[6]), .reset(Reset));  // open: Qn, preset, en
  D_Flip_Flop d_ff_11 (.clk(clock), .D(multiplexer_1_out[5]), .Q(rOut[5]), .reset(Reset));  // open: Qn, preset, en
  D_Flip_Flop d_ff_12 (.clk(clock), .D(multiplexer_1_out[4]), .Q(rOut[4]), .reset(Reset));  // open: Qn, preset, en
  D_Flip_Flop d_ff_13 (.clk(clock), .D(multiplexer_1_out[3]), .Q(rOut[3]), .reset(Reset));  // open: Qn, preset, en
  D_Flip_Flop d_ff_14 (.clk(clock), .D(multiplexer_1_out[2]), .Q(rOut[2]), .reset(Reset));  // open: Qn, preset, en
  D_Flip_Flop d_ff_15 (.clk(clock), .D(multiplexer_1_out[1]), .Q(rOut[1]), .reset(Reset));  // open: Qn, preset, en
  D_Flip_Flop d_ff_16 (.clk(clock), .D(multiplexer_1_out[0]), .Q(rOut[0]), .reset(Reset));  // open: Qn, preset, en

  // Other names for the same wires on the sheet: clk = clock; ot[15:0] = rOut; ree = Reset
endmodule

module RegisterFile (
  input  reset,
  input  clk,
  input  [15:0] WriteData,
  input  [2:0] ReadReg1,
  input  [2:0] ReadReg2,
  input  WE,
  input  [2:0] rd,
  output [15:0] ReadData1,
  output [15:0] ReadData2
);

  wire and_1_out, and_2_out, and_3_out, and_4_out, and_5_out, and_6_out, and_7_out, and_8_out,
       decoder_2_out0, decoder_2_out1, decoder_2_out2, decoder_2_out3, decoder_2_out4, decoder_2_out5,
       decoder_2_out6, decoder_2_out7, decoder_3_out0, decoder_3_out1, decoder_3_out2, decoder_3_out3,
       decoder_3_out4, decoder_3_out5, decoder_3_out6, decoder_3_out7, or_1_out, or_2_out, or_3_out,
       or_4_out, or_5_out, or_6_out, or_7_out, w0, w1, w2, w3, w4, w5, w6, w7;
  wire [15:0] five, four, one, sev, six, three, two, zero;

  assign ReadData2 = decoder_2_out0 ? zero : 16'bz;  // Controlled_Buffer controlled_buffer_1
  assign ReadData2 = decoder_2_out2 ? two : 16'bz;  // Controlled_Buffer controlled_buffer_2
  assign ReadData2 = decoder_2_out1 ? one : 16'bz;  // Controlled_Buffer controlled_buffer_3
  Decoder #(.select(3)) decoder_1 (
    .out0(w0), .out1(w1), .out2(w2), .out3(w3), .out4(w4), .out5(w5), .out6(w6), .out7(w7), .sel(rd),
    .en(1'b1));
  assign ReadData2 = decoder_2_out5 ? five : 16'bz;  // Controlled_Buffer controlled_buffer_4
  assign ReadData2 = decoder_2_out4 ? four : 16'bz;  // Controlled_Buffer controlled_buffer_5
  assign ReadData2 = decoder_2_out3 ? three : 16'bz;  // Controlled_Buffer controlled_buffer_6
  Decoder #(.select(3)) decoder_2 (
    .out0(decoder_2_out0), .out1(decoder_2_out1), .out2(decoder_2_out2), .out3(decoder_2_out3),
    .out4(decoder_2_out4), .out5(decoder_2_out5), .out6(decoder_2_out6), .out7(decoder_2_out7),
    .sel(ReadReg2), .en(1'b1));
  assign ReadData2 = decoder_2_out7 ? sev : 16'bz;  // Controlled_Buffer controlled_buffer_7
  assign ReadData2 = decoder_2_out6 ? six : 16'bz;  // Controlled_Buffer controlled_buffer_8
  register r0 (.rIn({16{1'b0}}), .clock(clk), .Reset(reset), .wEnable(and_1_out), .rOut(zero));
  and and_1 (and_1_out, 1'b0, w0);
  and and_2 (and_2_out, WE, w1);
  or or_1 (or_1_out, and_2_out, reset);
  register r1 (.rIn(WriteData), .clock(clk), .Reset(reset), .wEnable(or_1_out), .rOut(one));
  // Probe on zero
  register r2 (.rIn(WriteData), .clock(clk), .Reset(reset), .wEnable(or_2_out), .rOut(two));
  // Probe on one
  // Probe on two
  and and_3 (and_3_out, WE, w2);
  or or_2 (or_2_out, and_3_out, reset);
  // Probe on three
  and and_4 (and_4_out, WE, w3);
  or or_3 (or_3_out, and_4_out, reset);
  register r3_2 (.rIn(WriteData), .clock(clk), .Reset(reset), .wEnable(or_3_out), .rOut(three));
  // Probe on five
  // Probe on four
  and and_5 (and_5_out, WE, w4);
  or or_4 (or_4_out, and_5_out, reset);
  register r4_2 (.rIn(WriteData), .clock(clk), .Reset(reset), .wEnable(or_4_out), .rOut(four));
  // Probe on six
  // Probe on sev
  and and_6 (and_6_out, WE, w5);
  or or_5 (or_5_out, and_6_out, reset);
  register r5_2 (.rIn(WriteData), .clock(clk), .Reset(reset), .wEnable(or_5_out), .rOut(five));
  assign ReadData1 = decoder_3_out2 ? two : 16'bz;  // Controlled_Buffer controlled_buffer_9
  assign ReadData1 = decoder_3_out1 ? one : 16'bz;  // Controlled_Buffer controlled_buffer_10
  assign ReadData1 = decoder_3_out0 ? zero : 16'bz;  // Controlled_Buffer controlled_buffer_11
  and and_7 (and_7_out, WE, w6);
  or or_6 (or_6_out, and_7_out, reset);
  register r6_2 (.rIn(WriteData), .clock(clk), .Reset(reset), .wEnable(or_6_out), .rOut(six));
  assign ReadData1 = decoder_3_out5 ? five : 16'bz;  // Controlled_Buffer controlled_buffer_12
  assign ReadData1 = decoder_3_out4 ? four : 16'bz;  // Controlled_Buffer controlled_buffer_13
  assign ReadData1 = decoder_3_out3 ? three : 16'bz;  // Controlled_Buffer controlled_buffer_14
  Decoder #(.select(3)) decoder_3 (
    .out0(decoder_3_out0), .out1(decoder_3_out1), .out2(decoder_3_out2), .out3(decoder_3_out3),
    .out4(decoder_3_out4), .out5(decoder_3_out5), .out6(decoder_3_out6), .out7(decoder_3_out7),
    .sel(ReadReg1), .en(1'b1));
  assign ReadData1 = decoder_3_out7 ? sev : 16'bz;  // Controlled_Buffer controlled_buffer_15
  assign ReadData1 = decoder_3_out6 ? six : 16'bz;  // Controlled_Buffer controlled_buffer_16
  and and_8 (and_8_out, WE, w7);
  or or_7 (or_7_out, and_8_out, reset);
  register r7_2 (.rIn(WriteData), .clock(clk), .Reset(reset), .wEnable(or_7_out), .rOut(sev));

  // Other names for the same wires on the sheet: clkT = clk; reg1Num[2:0] = ReadReg1; reg2Num[2:0] = ReadReg2;
  //   wvalT[15:0] = WriteData
endmodule

module add (
  input  cin,
  input  a,
  input  b,
  output sum,
  output carry
);

  wire and_1_out, and_2_out, xor_1_out;

  xor xor_1 (xor_1_out, a, b);
  and and_1 (and_1_out, b, a);
  and and_2 (and_2_out, cin, xor_1_out);
  xor xor_2 (sum, cin, xor_1_out);
  or or_1 (carry, and_2_out, and_1_out);

  // Notes on the sheet:
  //   carry
endmodule

module addsub (
  input  [15:0] A,
  input  [15:0] B,
  input  sub,
  output ovf,
  output [15:0] result
);

  wire add_1_carry, add_2_carry, add_3_carry, add_4_carry, add_5_carry, add_6_carry, add_7_carry,
       add_8_carry, add_9_carry, add_10_carry, add_11_carry, add_12_carry, add_13_carry, add_14_carry,
       add_15_carry, add_16_carry, multiplexer_2_out;
  wire [15:0] multiplexer_1_out, not_1_out;

  add add_1 (.cin(add_2_carry), .a(A[15]), .b(multiplexer_1_out[15]), .sum(result[15]), .carry(add_1_carry));
  xor xor_1 (ovf, add_2_carry, add_1_carry);
  add add_2 (.cin(add_3_carry), .a(A[14]), .b(multiplexer_1_out[14]), .sum(result[14]), .carry(add_2_carry));
  add add_3 (.cin(add_4_carry), .a(A[13]), .b(multiplexer_1_out[13]), .sum(result[13]), .carry(add_3_carry));
  assign not_1_out = ~B;  // NOT_Gate not_1, 16 bits wide
  add add_4 (.cin(add_5_carry), .a(A[12]), .b(multiplexer_1_out[12]), .sum(result[12]), .carry(add_4_carry));
  add add_5 (.cin(add_6_carry), .a(A[11]), .b(multiplexer_1_out[11]), .sum(result[11]), .carry(add_5_carry));
  Multiplexer #(.width(16)) multiplexer_1 (.in0(B), .in1(not_1_out), .out(multiplexer_1_out), .sel(sub));  // open: en
  add add_6 (.cin(add_7_carry), .a(A[10]), .b(multiplexer_1_out[10]), .sum(result[10]), .carry(add_6_carry));
  add add_7 (.cin(add_8_carry), .a(A[9]), .b(multiplexer_1_out[9]), .sum(result[9]), .carry(add_7_carry));
  add add_8 (.cin(add_9_carry), .a(A[8]), .b(multiplexer_1_out[8]), .sum(result[8]), .carry(add_8_carry));
  add add_9 (.cin(add_10_carry), .a(A[7]), .b(multiplexer_1_out[7]), .sum(result[7]), .carry(add_9_carry));
  add add_10 (.cin(add_11_carry), .a(A[6]), .b(multiplexer_1_out[6]), .sum(result[6]), .carry(add_10_carry));
  add add_11 (.cin(add_12_carry), .a(A[5]), .b(multiplexer_1_out[5]), .sum(result[5]), .carry(add_11_carry));
  add add_12 (.cin(add_13_carry), .a(A[4]), .b(multiplexer_1_out[4]), .sum(result[4]), .carry(add_12_carry));
  add add_13 (.cin(add_14_carry), .a(A[3]), .b(multiplexer_1_out[3]), .sum(result[3]), .carry(add_13_carry));
  add add_14 (.cin(add_15_carry), .a(A[2]), .b(multiplexer_1_out[2]), .sum(result[2]), .carry(add_14_carry));
  add add_15 (.cin(add_16_carry), .a(A[1]), .b(multiplexer_1_out[1]), .sum(result[1]), .carry(add_15_carry));
  add add_16 (.cin(multiplexer_2_out), .a(A[0]), .b(multiplexer_1_out[0]), .sum(result[0]), .carry(add_16_carry));
  Multiplexer multiplexer_2 (.in0(1'b0), .in1(1'b1), .out(multiplexer_2_out), .sel(sub));  // open: en
endmodule

module negator (
  input  [15:0] nIn,
  output [15:0] nOut
);

  assign nOut = ~nIn;  // NOT_Gate not_1, 16 bits wide
endmodule

module xorer (
  input  [15:0] xIn1,
  input  [15:0] xIn2,
  output [15:0] xOut
);

  assign xOut = xIn1 ^ xIn2;  // XOR_Gate xor_1, 16 bits wide
endmodule

module rshifter (
  input  [15:0] in,
  input  [2:0] shamt,
  output [15:0] out_3
);

  wire multiplexer_1_out, multiplexer_2_out, multiplexer_3_out, multiplexer_4_out, multiplexer_5_out,
       multiplexer_6_out, multiplexer_7_out, multiplexer_8_out, multiplexer_9_out, multiplexer_10_out,
       multiplexer_11_out, multiplexer_12_out, multiplexer_13_out, multiplexer_14_out, multiplexer_15_out,
       multiplexer_16_out, multiplexer_17_out, multiplexer_18_out, multiplexer_19_out, multiplexer_20_out,
       multiplexer_21_out, multiplexer_22_out, multiplexer_23_out, multiplexer_24_out, multiplexer_25_out,
       multiplexer_26_out, multiplexer_27_out, multiplexer_28_out, multiplexer_29_out, multiplexer_30_out,
       multiplexer_31_out, multiplexer_32_out;

  Multiplexer #(.enable("false")) multiplexer_1 (.in0(in[0]), .in1(in[1]), .out(multiplexer_1_out), .sel(shamt[0]));
  Multiplexer #(.enable("false")) multiplexer_2 (.in0(in[1]), .in1(in[2]), .out(multiplexer_2_out), .sel(shamt[0]));
  Multiplexer #(.enable("false")) multiplexer_3 (.in0(in[2]), .in1(in[3]), .out(multiplexer_3_out), .sel(shamt[0]));
  Multiplexer #(.enable("false")) multiplexer_4 (.in0(in[3]), .in1(in[4]), .out(multiplexer_4_out), .sel(shamt[0]));
  Multiplexer #(.enable("false")) multiplexer_5 (.in0(in[4]), .in1(in[5]), .out(multiplexer_5_out), .sel(shamt[0]));
  Multiplexer #(.enable("false")) multiplexer_6 (.in0(in[5]), .in1(in[6]), .out(multiplexer_6_out), .sel(shamt[0]));
  Multiplexer #(.enable("false")) multiplexer_7 (.in0(in[6]), .in1(in[7]), .out(multiplexer_7_out), .sel(shamt[0]));
  Multiplexer #(.enable("false")) multiplexer_8 (.in0(in[7]), .in1(in[8]), .out(multiplexer_8_out), .sel(shamt[0]));
  Multiplexer #(.enable("false")) multiplexer_9 (.in0(in[8]), .in1(in[9]), .out(multiplexer_9_out), .sel(shamt[0]));
  Multiplexer #(.enable("false")) multiplexer_10 (.in0(in[9]), .in1(in[10]), .out(multiplexer_10_out), .sel(shamt[0]));
  Multiplexer #(.enable("false")) multiplexer_11 (.in0(in[10]), .in1(in[11]), .out(multiplexer_11_out), .sel(shamt[0]));
  Multiplexer #(.enable("false")) multiplexer_12 (.in0(in[11]), .in1(in[12]), .out(multiplexer_12_out), .sel(shamt[0]));
  Multiplexer #(.enable("false")) multiplexer_13 (.in0(in[12]), .in1(in[13]), .out(multiplexer_13_out), .sel(shamt[0]));
  Multiplexer #(.enable("false")) multiplexer_14 (.in0(in[13]), .in1(in[14]), .out(multiplexer_14_out), .sel(shamt[0]));
  Multiplexer #(.enable("false")) multiplexer_15 (.in0(in[14]), .in1(in[15]), .out(multiplexer_15_out), .sel(shamt[0]));
  Multiplexer #(.enable("false")) multiplexer_16 (.in0(in[15]), .in1(in[15]), .out(multiplexer_16_out), .sel(shamt[0]));
  Multiplexer #(.enable("false")) multiplexer_17 (
    .in0(multiplexer_1_out), .in1(multiplexer_3_out), .out(multiplexer_17_out), .sel(shamt[1]));
  Multiplexer #(.enable("false")) multiplexer_18 (
    .in0(multiplexer_2_out), .in1(multiplexer_4_out), .out(multiplexer_18_out), .sel(shamt[1]));
  Multiplexer #(.enable("false")) multiplexer_19 (
    .in0(multiplexer_3_out), .in1(multiplexer_5_out), .out(multiplexer_19_out), .sel(shamt[1]));
  Multiplexer #(.enable("false")) multiplexer_20 (
    .in0(multiplexer_4_out), .in1(multiplexer_6_out), .out(multiplexer_20_out), .sel(shamt[1]));
  Multiplexer #(.enable("false")) multiplexer_21 (
    .in0(multiplexer_5_out), .in1(multiplexer_7_out), .out(multiplexer_21_out), .sel(shamt[1]));
  Multiplexer #(.enable("false")) multiplexer_22 (
    .in0(multiplexer_6_out), .in1(multiplexer_8_out), .out(multiplexer_22_out), .sel(shamt[1]));
  Multiplexer #(.enable("false")) multiplexer_23 (
    .in0(multiplexer_7_out), .in1(multiplexer_9_out), .out(multiplexer_23_out), .sel(shamt[1]));
  Multiplexer #(.enable("false")) multiplexer_24 (
    .in0(multiplexer_8_out), .in1(multiplexer_10_out), .out(multiplexer_24_out), .sel(shamt[1]));
  Multiplexer #(.enable("false")) multiplexer_25 (
    .in0(multiplexer_9_out), .in1(multiplexer_11_out), .out(multiplexer_25_out), .sel(shamt[1]));
  Multiplexer #(.enable("false")) multiplexer_26 (
    .in0(multiplexer_10_out), .in1(multiplexer_12_out), .out(multiplexer_26_out), .sel(shamt[1]));
  Multiplexer #(.enable("false")) multiplexer_27 (
    .in0(multiplexer_11_out), .in1(multiplexer_13_out), .out(multiplexer_27_out), .sel(shamt[1]));
  Multiplexer #(.enable("false")) multiplexer_28 (
    .in0(multiplexer_12_out), .in1(multiplexer_14_out), .out(multiplexer_28_out), .sel(shamt[1]));
  Multiplexer #(.enable("false")) multiplexer_29 (
    .in0(multiplexer_13_out), .in1(multiplexer_15_out), .out(multiplexer_29_out), .sel(shamt[1]));
  Multiplexer #(.enable("false")) multiplexer_30 (
    .in0(multiplexer_14_out), .in1(multiplexer_16_out), .out(multiplexer_30_out), .sel(shamt[1]));
  Multiplexer #(.enable("false")) multiplexer_31 (
    .in0(multiplexer_15_out), .in1(in[15]), .out(multiplexer_31_out), .sel(shamt[1]));
  Multiplexer #(.enable("false")) multiplexer_32 (
    .in0(multiplexer_16_out), .in1(in[15]), .out(multiplexer_32_out), .sel(shamt[1]));
  Multiplexer #(.enable("false")) multiplexer_33 (
    .in0(multiplexer_17_out), .in1(multiplexer_21_out), .out(out_3[0]), .sel(shamt[2]));
  Multiplexer #(.enable("false")) multiplexer_34 (
    .in0(multiplexer_18_out), .in1(multiplexer_22_out), .out(out_3[1]), .sel(shamt[2]));
  Multiplexer #(.enable("false")) multiplexer_35 (
    .in0(multiplexer_19_out), .in1(multiplexer_23_out), .out(out_3[2]), .sel(shamt[2]));
  Multiplexer #(.enable("false")) multiplexer_36 (
    .in0(multiplexer_20_out), .in1(multiplexer_24_out), .out(out_3[3]), .sel(shamt[2]));
  Multiplexer #(.enable("false")) multiplexer_37 (
    .in0(multiplexer_21_out), .in1(multiplexer_25_out), .out(out_3[4]), .sel(shamt[2]));
  Multiplexer #(.enable("false")) multiplexer_38 (
    .in0(multiplexer_22_out), .in1(multiplexer_26_out), .out(out_3[5]), .sel(shamt[2]));
  Multiplexer #(.enable("false")) multiplexer_39 (
    .in0(multiplexer_26_out), .in1(multiplexer_27_out), .out(out_3[6]), .sel(shamt[2]));
  Multiplexer #(.enable("false")) multiplexer_40 (
    .in0(multiplexer_24_out), .in1(multiplexer_28_out), .out(out_3[7]), .sel(shamt[2]));
  Multiplexer #(.enable("false")) multiplexer_41 (
    .in0(multiplexer_25_out), .in1(multiplexer_29_out), .out(out_3[8]), .sel(shamt[2]));
  Multiplexer #(.enable("false")) multiplexer_42 (
    .in0(multiplexer_26_out), .in1(multiplexer_30_out), .out(out_3[9]), .sel(shamt[2]));
  Multiplexer #(.enable("false")) multiplexer_43 (
    .in0(multiplexer_27_out), .in1(multiplexer_31_out), .out(out_3[10]), .sel(shamt[2]));
  Multiplexer #(.enable("false")) multiplexer_44 (
    .in0(multiplexer_28_out), .in1(multiplexer_32_out), .out(out_3[11]), .sel(shamt[2]));
  Multiplexer #(.enable("false")) multiplexer_45 (
    .in0(multiplexer_29_out), .in1(in[15]), .out(out_3[12]), .sel(shamt[2]));
  Multiplexer #(.enable("false")) multiplexer_46 (
    .in0(multiplexer_30_out), .in1(in[15]), .out(out_3[13]), .sel(shamt[2]));
  Multiplexer #(.enable("false")) multiplexer_47 (
    .in0(multiplexer_31_out), .in1(in[15]), .out(out_3[14]), .sel(shamt[2]));
  Multiplexer #(.enable("false")) multiplexer_48 (
    .in0(multiplexer_32_out), .in1(in[15]), .out(out_3[15]), .sel(shamt[2]));

  // Other names for the same wires on the sheet: _0 = in[0]; _1 = in[1]; _2 = in[2]; _3 = in[3]; _4 = in[4];
  //   _5 = in[5]; _6 = in[6]; _7 = in[7]; _8 = in[8]; _9 = in[9]; _10 = in[10]; _11 = in[11]; _12 = in[12];
  //   _13 = in[13]; _14 = in[14]; _15 = in[15]; s0 = shamt[0]; s1 = shamt[1]; s2 = shamt[2]
endmodule

module ALU (
  input  [2:0] shAmt,
  input  [15:0] InputData1,
  input  [15:0] InputData2,
  input  [3:0] OpCode,
  output [15:0] out
);

  wire decoder_1_out0, decoder_1_out1, decoder_1_out2, decoder_1_out3, decoder_1_out4, decoder_1_out5,
       decoder_1_out6, decoder_1_out7, decoder_1_out8;
  wire [15:0] addout, lsout, nOut, rsout, subout, xorout;

  addsub addsub_1 (.result(addout), .sub(1'b0), .A(InputData1), .B(InputData2));  // open: ovf
  lshifter lshifter_1 (.in(InputData1), .shamt(shAmt), .out(lsout));
  negator negator_1 (.nIn(InputData1), .nOut(nOut));
  addsub addsub_2 (.result(subout), .sub(1'b1), .A(InputData1), .B(InputData2));  // open: ovf
  rshifter rshifter_1 (.in(InputData1), .shamt(shAmt), .out_3(rsout));
  xorer xorer_1 (.xIn1(InputData1), .xIn2(InputData2), .xOut(xorout));
  assign out = decoder_1_out8 ? addout : 16'bz;  // Controlled_Buffer controlled_buffer_1
  assign out = decoder_1_out7 ? addout : 16'bz;  // Controlled_Buffer controlled_buffer_2
  assign out = decoder_1_out6 ? rsout : 16'bz;  // Controlled_Buffer controlled_buffer_3
  assign out = decoder_1_out5 ? lsout : 16'bz;  // Controlled_Buffer controlled_buffer_4
  assign out = decoder_1_out4 ? xorout : 16'bz;  // Controlled_Buffer controlled_buffer_5
  assign out = decoder_1_out3 ? nOut : 16'bz;  // Controlled_Buffer controlled_buffer_6
  assign out = decoder_1_out2 ? subout : 16'bz;  // Controlled_Buffer controlled_buffer_7
  assign out = decoder_1_out1 ? addout : 16'bz;  // Controlled_Buffer controlled_buffer_8
  assign out = decoder_1_out0 ? addout : 16'bz;  // Controlled_Buffer controlled_buffer_9
  Decoder #(.select(4)) decoder_1 (
    .out0(decoder_1_out0), .out1(decoder_1_out1), .out2(decoder_1_out2), .out3(decoder_1_out3),
    .out4(decoder_1_out4), .out5(decoder_1_out5), .out6(decoder_1_out6), .out7(decoder_1_out7),
    .out8(decoder_1_out8), .sel(OpCode), .en(1'b1));  // open: out9, out10, out11, out12, out13, out14, out15

  // Other names for the same wires on the sheet: in1[15:0] = InputData1; in2[15:0] = InputData2; sh[2:0] = shAmt
endmodule

module lshifter (
  input  [15:0] in,
  input  [2:0] shamt,
  output [15:0] out
);

  wire multiplexer_1_out, multiplexer_2_out, multiplexer_3_out, multiplexer_4_out, multiplexer_5_out,
       multiplexer_6_out, multiplexer_7_out, multiplexer_8_out, multiplexer_9_out, multiplexer_10_out,
       multiplexer_11_out, multiplexer_12_out, multiplexer_13_out, multiplexer_14_out, multiplexer_15_out,
       multiplexer_16_out, multiplexer_17_out, multiplexer_18_out, multiplexer_19_out, multiplexer_20_out,
       multiplexer_21_out, multiplexer_22_out, multiplexer_23_out, multiplexer_24_out, multiplexer_25_out,
       multiplexer_26_out, multiplexer_27_out, multiplexer_28_out, multiplexer_29_out, multiplexer_30_out,
       multiplexer_31_out, multiplexer_32_out;

  Multiplexer #(.enable("false")) multiplexer_1 (.in0(in[0]), .in1(1'b0), .out(multiplexer_1_out), .sel(shamt[0]));
  Multiplexer #(.enable("false")) multiplexer_2 (.in0(in[1]), .in1(in[0]), .out(multiplexer_2_out), .sel(shamt[0]));
  Multiplexer #(.enable("false")) multiplexer_3 (.in0(in[2]), .in1(in[1]), .out(multiplexer_3_out), .sel(shamt[0]));
  Multiplexer #(.enable("false")) multiplexer_4 (.in0(in[3]), .in1(in[2]), .out(multiplexer_4_out), .sel(shamt[0]));
  Multiplexer #(.enable("false")) multiplexer_5 (.in0(in[4]), .in1(in[3]), .out(multiplexer_5_out), .sel(shamt[0]));
  Multiplexer #(.enable("false")) multiplexer_6 (.in0(in[5]), .in1(in[4]), .out(multiplexer_6_out), .sel(shamt[0]));
  Multiplexer #(.enable("false")) multiplexer_7 (.in0(in[6]), .in1(in[5]), .out(multiplexer_7_out), .sel(shamt[0]));
  Multiplexer #(.enable("false")) multiplexer_8 (.in0(in[7]), .in1(in[6]), .out(multiplexer_8_out), .sel(shamt[0]));
  Multiplexer #(.enable("false")) multiplexer_9 (.in0(in[8]), .in1(in[7]), .out(multiplexer_9_out), .sel(shamt[0]));
  Multiplexer #(.enable("false")) multiplexer_10 (.in0(in[9]), .in1(in[8]), .out(multiplexer_10_out), .sel(shamt[0]));
  Multiplexer #(.enable("false")) multiplexer_11 (.in0(in[10]), .in1(in[9]), .out(multiplexer_11_out), .sel(shamt[0]));
  Multiplexer #(.enable("false")) multiplexer_12 (.in0(in[11]), .in1(in[10]), .out(multiplexer_12_out), .sel(shamt[0]));
  Multiplexer #(.enable("false")) multiplexer_13 (.in0(in[12]), .in1(in[11]), .out(multiplexer_13_out), .sel(shamt[0]));
  Multiplexer #(.enable("false")) multiplexer_14 (.in0(in[13]), .in1(in[12]), .out(multiplexer_14_out), .sel(shamt[0]));
  Multiplexer #(.enable("false")) multiplexer_15 (.in0(in[14]), .in1(in[13]), .out(multiplexer_15_out), .sel(shamt[0]));
  Multiplexer #(.enable("false")) multiplexer_16 (.in0(in[15]), .in1(in[14]), .out(multiplexer_16_out), .sel(shamt[0]));
  Multiplexer #(.enable("false")) multiplexer_17 (
    .in0(multiplexer_1_out), .in1(1'b0), .out(multiplexer_17_out), .sel(shamt[1]));
  Multiplexer #(.enable("false")) multiplexer_18 (
    .in0(multiplexer_2_out), .in1(1'b0), .out(multiplexer_18_out), .sel(shamt[1]));
  Multiplexer #(.enable("false")) multiplexer_19 (
    .in0(multiplexer_3_out), .in1(multiplexer_1_out), .out(multiplexer_19_out), .sel(shamt[1]));
  Multiplexer #(.enable("false")) multiplexer_20 (
    .in0(multiplexer_4_out), .in1(multiplexer_2_out), .out(multiplexer_20_out), .sel(shamt[1]));
  Multiplexer #(.enable("false")) multiplexer_21 (
    .in0(multiplexer_5_out), .in1(multiplexer_3_out), .out(multiplexer_21_out), .sel(shamt[1]));
  Multiplexer #(.enable("false")) multiplexer_22 (
    .in0(multiplexer_6_out), .in1(multiplexer_4_out), .out(multiplexer_22_out), .sel(shamt[1]));
  Multiplexer #(.enable("false")) multiplexer_23 (
    .in0(multiplexer_7_out), .in1(multiplexer_5_out), .out(multiplexer_23_out), .sel(shamt[1]));
  Multiplexer #(.enable("false")) multiplexer_24 (
    .in0(multiplexer_8_out), .in1(multiplexer_6_out), .out(multiplexer_24_out), .sel(shamt[1]));
  Multiplexer #(.enable("false")) multiplexer_25 (
    .in0(multiplexer_9_out), .in1(multiplexer_7_out), .out(multiplexer_25_out), .sel(shamt[1]));
  Multiplexer #(.enable("false")) multiplexer_26 (
    .in0(multiplexer_10_out), .in1(multiplexer_8_out), .out(multiplexer_26_out), .sel(shamt[1]));
  Multiplexer #(.enable("false")) multiplexer_27 (
    .in0(multiplexer_11_out), .in1(multiplexer_9_out), .out(multiplexer_27_out), .sel(shamt[1]));
  Multiplexer #(.enable("false")) multiplexer_28 (
    .in0(multiplexer_12_out), .in1(multiplexer_10_out), .out(multiplexer_28_out), .sel(shamt[1]));
  Multiplexer #(.enable("false")) multiplexer_29 (
    .in0(multiplexer_13_out), .in1(multiplexer_11_out), .out(multiplexer_29_out), .sel(shamt[1]));
  Multiplexer #(.enable("false")) multiplexer_30 (
    .in0(multiplexer_14_out), .in1(multiplexer_12_out), .out(multiplexer_30_out), .sel(shamt[1]));
  Multiplexer #(.enable("false")) multiplexer_31 (
    .in0(multiplexer_15_out), .in1(multiplexer_13_out), .out(multiplexer_31_out), .sel(shamt[1]));
  Multiplexer #(.enable("false")) multiplexer_32 (
    .in0(multiplexer_16_out), .in1(multiplexer_14_out), .out(multiplexer_32_out), .sel(shamt[1]));
  Multiplexer #(.enable("false")) multiplexer_33 (.in0(multiplexer_17_out), .in1(1'b0), .out(out[0]), .sel(shamt[2]));
  Multiplexer #(.enable("false")) multiplexer_34 (.in0(multiplexer_18_out), .in1(1'b0), .out(out[1]), .sel(shamt[2]));
  Multiplexer #(.enable("false")) multiplexer_35 (.in0(multiplexer_19_out), .in1(1'b0), .out(out[2]), .sel(shamt[2]));
  Multiplexer #(.enable("false")) multiplexer_36 (.in0(multiplexer_20_out), .in1(1'b0), .out(out[3]), .sel(shamt[2]));
  Multiplexer #(.enable("false")) multiplexer_37 (
    .in0(multiplexer_21_out), .in1(multiplexer_17_out), .out(out[4]), .sel(shamt[2]));
  Multiplexer #(.enable("false")) multiplexer_38 (
    .in0(multiplexer_22_out), .in1(multiplexer_18_out), .out(out[5]), .sel(shamt[2]));
  Multiplexer #(.enable("false")) multiplexer_39 (
    .in0(multiplexer_23_out), .in1(multiplexer_19_out), .out(out[6]), .sel(shamt[2]));
  Multiplexer #(.enable("false")) multiplexer_40 (
    .in0(multiplexer_24_out), .in1(multiplexer_20_out), .out(out[7]), .sel(shamt[2]));
  Multiplexer #(.enable("false")) multiplexer_41 (
    .in0(multiplexer_25_out), .in1(multiplexer_21_out), .out(out[8]), .sel(shamt[2]));
  Multiplexer #(.enable("false")) multiplexer_42 (
    .in0(multiplexer_26_out), .in1(multiplexer_22_out), .out(out[9]), .sel(shamt[2]));
  Multiplexer #(.enable("false")) multiplexer_43 (
    .in0(multiplexer_27_out), .in1(multiplexer_23_out), .out(out[10]), .sel(shamt[2]));
  Multiplexer #(.enable("false")) multiplexer_44 (
    .in0(multiplexer_28_out), .in1(multiplexer_24_out), .out(out[11]), .sel(shamt[2]));
  Multiplexer #(.enable("false")) multiplexer_45 (
    .in0(multiplexer_29_out), .in1(multiplexer_25_out), .out(out[12]), .sel(shamt[2]));
  Multiplexer #(.enable("false")) multiplexer_46 (
    .in0(multiplexer_30_out), .in1(multiplexer_26_out), .out(out[13]), .sel(shamt[2]));
  Multiplexer #(.enable("false")) multiplexer_47 (
    .in0(multiplexer_31_out), .in1(multiplexer_27_out), .out(out[14]), .sel(shamt[2]));
  Multiplexer #(.enable("false")) multiplexer_48 (
    .in0(multiplexer_32_out), .in1(multiplexer_28_out), .out(out[15]), .sel(shamt[2]));

  // Other names for the same wires on the sheet: _0 = in[0]; _1 = in[1]; _2 = in[2]; _3 = in[3]; _4 = in[4];
  //   _5 = in[5]; _6 = in[6]; _7 = in[7]; _8 = in[8]; _9 = in[9]; _10 = in[10]; _11 = in[11]; _12 = in[12];
  //   _13 = in[13]; _14 = in[14]; _15 = in[15]; s0 = shamt[0]; s1 = shamt[1]; s2 = shamt[2]
endmodule

module signextender (
  input  [5:0] immed,
  output [15:0] out
);

  buf buffer_1 (out[0], immed[0]);
  buf buffer_2 (out[1], immed[1]);
  buf buffer_3 (out[2], immed[2]);
  buf buffer_4 (out[3], immed[3]);
  buf buffer_5 (out[4], immed[4]);
  buf buffer_6 (out[15], immed[5]);

  assign out[14:5] = {10{out[15]}};
endmodule

module ctrl (
  input  [3:0] OpCode,
  output Rwe,
  output J,
  output BR,
  output DMwe,
  output Rwd,
  output Rdst,
  output IN,
  output OUT,
  output JAL,
  output Itp,
  output JR
);

  wire add, addi, blt, bne, \not , not_1_out, not_2_out, not_3_out, not_4_out, not_5_out, not_6_out,
       not_7_out, not_8_out, not_9_out, not_10_out, not_11_out, not_12_out, not_13_out, not_14_out,
       not_15_out, not_16_out, not_17_out, not_18_out, not_19_out, not_20_out, not_21_out, not_22_out,
       not_23_out, not_24_out, not_25_out, not_26_out, not_27_out, not_28_out, not_30_out, not_31_out,
       not_32_out, not_33_out, sll, srl, sub, \xor ;

  or or_1 (Rwe, IN, JAL, add, addi, sub, \not , sll, srl, Rwd, DMwe, \xor );
  not not_1 (not_1_out, OpCode[0]);
  not not_2 (not_2_out, OpCode[1]);
  not not_3 (not_3_out, OpCode[2]);
  not not_4 (not_4_out, OpCode[3]);
  not not_5 (not_5_out, OpCode[0]);
  not not_6 (not_6_out, OpCode[1]);
  not not_7 (not_7_out, OpCode[3]);
  not not_8 (not_8_out, OpCode[0]);
  not not_9 (not_9_out, OpCode[1]);
  not not_10 (not_10_out, OpCode[2]);
  not not_11 (not_11_out, OpCode[0]);
  not not_12 (not_12_out, OpCode[1]);
  and add0000 (add, not_1_out, not_2_out, not_3_out, not_4_out);
  and xor0100 (\xor , not_5_out, not_6_out, OpCode[2], not_7_out);
  and sw1000 (DMwe, not_8_out, not_9_out, not_10_out, OpCode[3]);
  and jr1100 (JR, not_11_out, not_12_out, OpCode[2], OpCode[3]);
  or or_2 (BR, bne, blt);
  not not_13 (not_13_out, OpCode[1]);
  not not_14 (not_14_out, OpCode[2]);
  not not_15 (not_15_out, OpCode[3]);
  not not_16 (not_16_out, OpCode[1]);
  not not_17 (not_17_out, OpCode[3]);
  not not_18 (not_18_out, OpCode[1]);
  not not_19 (not_19_out, OpCode[2]);
  not not_20 (not_20_out, OpCode[1]);
  and addi0001 (addi, OpCode[0], not_13_out, not_14_out, not_15_out);
  and sll0101 (sll, OpCode[0], not_16_out, OpCode[2], not_17_out);
  and bne1001 (bne, OpCode[0], not_18_out, not_19_out, OpCode[3]);
  and jal1101 (JAL, OpCode[0], not_20_out, OpCode[2], OpCode[3]);
  or or_3 (Itp, bne, addi, blt, Rwd, IN, DMwe, OUT);
  not not_21 (not_21_out, OpCode[0]);
  not not_22 (not_22_out, OpCode[2]);
  not not_23 (not_23_out, OpCode[3]);
  not not_24 (not_24_out, OpCode[0]);
  not not_25 (not_25_out, OpCode[3]);
  not not_26 (not_26_out, OpCode[0]);
  not not_27 (not_27_out, OpCode[2]);
  not not_28 (not_28_out, OpCode[0]);
  and sub0010 (sub, not_21_out, OpCode[1], not_22_out, not_23_out);
  and srl0110 (srl, not_24_out, OpCode[1], OpCode[2], not_25_out);
  and blt1010 (blt, not_26_out, OpCode[1], not_27_out, OpCode[3]);
  and inp1110 (IN, not_28_out, OpCode[1], OpCode[2], OpCode[3]);
  not not_29 (Rdst, Rwd);
  not not_30 (not_30_out, OpCode[2]);
  not not_31 (not_31_out, OpCode[3]);
  not not_32 (not_32_out, OpCode[3]);
  not not_33 (not_33_out, OpCode[2]);
  and not0011 (\not , OpCode[0], OpCode[1], not_30_out, not_31_out);
  and lw_0111 (Rwd, OpCode[0], OpCode[1], OpCode[2], not_32_out);
  and j1011 (J, OpCode[0], OpCode[1], not_33_out, OpCode[3]);
  and out1111 (OUT, OpCode[0], OpCode[1], OpCode[2], OpCode[3]);

  // Other names for the same wires on the sheet: input = IN; lw = Rwd; _0 = OpCode[0]; _1 = OpCode[1]; _2 = OpCode[2];
  //   _3 = OpCode[3]; output = OUT; sw = DMwe

  // Notes on the sheet:
  //   ReadWriteEnable
  //   Jump
  //   rtype
  //   Branch
  //   DataMemoryWriteEnable
  //   Match opcode
  //   ReadWriteDisable
endmodule

module checkeq (
  input  [15:0] in1,
  input  [15:0] in2,
  output out
);

  wire or_1_out, xor_1_out, xor_2_out, xor_3_out, xor_4_out, xor_5_out, xor_6_out, xor_7_out, xor_8_out,
       xor_9_out, xor_10_out, xor_11_out, xor_12_out, xor_13_out, xor_14_out, xor_15_out, xor_16_out;

  xor xor_1 (xor_1_out, in1[0], in2[0]);
  xor xor_2 (xor_2_out, in1[1], in2[1]);
  xor xor_3 (xor_3_out, in1[2], in2[2]);
  xor xor_4 (xor_4_out, in1[3], in2[3]);
  xor xor_5 (xor_5_out, in1[4], in2[4]);
  xor xor_6 (xor_6_out, in1[5], in2[5]);
  xor xor_7 (xor_7_out, in1[6], in2[6]);
  xor xor_8 (xor_8_out, in1[7], in2[7]);
  xor xor_9 (xor_9_out, in1[8], in2[8]);
  xor xor_10 (xor_10_out, in1[9], in2[9]);
  xor xor_11 (xor_11_out, in1[10], in2[10]);
  xor xor_12 (xor_12_out, in1[11], in2[11]);
  xor xor_13 (xor_13_out, in1[12], in2[12]);
  xor xor_14 (xor_14_out, in1[13], in2[13]);
  xor xor_15 (xor_15_out, in1[14], in2[14]);
  xor xor_16 (xor_16_out, in1[15], in2[15]);
  or or_1 (or_1_out, xor_1_out, xor_2_out, xor_3_out, xor_4_out, xor_5_out, xor_6_out, xor_7_out, xor_8_out, xor_9_out, xor_10_out, xor_11_out, xor_12_out, xor_13_out, xor_14_out, xor_15_out, xor_16_out);
  not not_1 (out, or_1_out);

  // Other names for the same wires on the sheet: _1 = in1[0]; _2 = in1[1]; _3 = in1[2]; _4 = in1[3]; _5 = in1[4];
  //   _6 = in1[5]; _7 = in1[6]; _8 = in1[7]; _9 = in1[8]; _10 = in1[9]; _11 = in1[10]; _12 = in1[11]; _13 = in1[12];
  //   _14 = in1[13]; _15 = in1[14]; _16 = in1[15]; a1 = in2[0]; a2 = in2[1]; a3 = in2[2]; a4 = in2[3]; a5 = in2[4];
  //   a6 = in2[5]; a7 = in2[6]; a8 = in2[7]; a9 = in2[8]; a10 = in2[9]; a11 = in2[10]; a12 = in2[11]; a13 = in2[12];
  //   a14 = in2[13]; a15 = in2[14]; a16 = in2[15]
endmodule

module checklt (
  input  [15:0] in1,
  input  [15:0] in2,
  output out
);

  Comparator #(.width(16)) comparator_1 (.a(in1), .b(in2), .lt(out));  // open: gt, eq

  // Other names for the same wires on the sheet: _1 = in1[0]; _2 = in1[1]; _3 = in1[2]; _4 = in1[3]; _5 = in1[4];
  //   _6 = in1[5]; _7 = in1[6]; _8 = in1[7]; _9 = in1[8]; _10 = in1[9]; _11 = in1[10]; _12 = in1[11]; _13 = in1[12];
  //   _14 = in1[13]; _15 = in1[14]; _16 = in1[15]; a1 = in2[0]; a2 = in2[1]; a3 = in2[2]; a4 = in2[3]; a5 = in2[4];
  //   a6 = in2[5]; a7 = in2[6]; a8 = in2[7]; a9 = in2[8]; a10 = in2[9]; a11 = in2[10]; a12 = in2[11]; a13 = in2[12];
  //   a14 = in2[13]; a15 = in2[14]; a16 = in2[15]
endmodule
